# Fritzing sketch finaal_circuit (saved by Fritzing 0.9.3b)
breadboards: 1

parts:
  Onderdeel1 = Arduino Mega 2560 (Rev3)
  LCD1 = LCD screen
  R1 = Resistor [tolerance=±5% resistance=220 package=THT]  # not connected
  R2 = Trimmer Potentiometer [maximum_resistance=10kΩ package=THT]
  CUI-enc1 = AMT103
  Part1 = KY-028 Digital Temperature Sensor Module [package="Breakout board"]
  Part2 = KY-011 Two Color LED Module [package="Breakout board"]
  R3 = Resistor [tolerance=±5% resistance=220 package=THT]
  R4 = Resistor [tolerance=±5% resistance=220 package=THT]
  Part3 = KY-022 Infrared Receiver Module [package="Breakout board"]
  Part4 = KY-018 Photoresistor Module [package="Breakout board"]
  Part5 = KY-015 Temperature & Humidity Sensor Module [package="Breakout board"]
  hc-sr1 = hc-sr04
  Part6 = KY-006 Passive Buzzer Module [package="Breakout board"]
  Water_Level_Sensor1 = Water Level Sensor
  J1 = Basic Servo

nets:
  N1: Onderdeel1.A0, Part1.A0
  N2: Onderdeel1.A2, Part4.S
  N3: Onderdeel1.A4, Water_Level_Sensor1.SIG
  GND: Onderdeel1.GND, LCD1.VSS, LCD1.R/W, LCD1.LED-, R2.leg1, CUI-enc1.GND, Part1.G, Part2.-, Part3.-, Part4.-, Part5.-, hc-sr1.GND, Part6.-, Water_Level_Sensor1.GND, J1.gnd
  N4: Onderdeel1.D12_PWM, LCD1.RS
  N5: Onderdeel1.D11_PWM, LCD1.E
  N6: Onderdeel1.D10_PWM, CUI-enc1.B
  N7: Onderdeel1.D9_PWM, CUI-enc1.A
  N8: Onderdeel1.D8_PWM, CUI-enc1.X
  VIN: Onderdeel1.5V, LCD1.VDD, R2.leg2, CUI-enc1.5V, Part1.+, Part3.Vin, Part4.Vin, Part5.Vin, hc-sr1.VCC, Water_Level_Sensor1.VCC, J1.vcc
  N9: Onderdeel1.D2_PWM, LCD1.DB7
  N10: Onderdeel1.D3_PWM, LCD1.DB6
  N11: Onderdeel1.D4_PWM, LCD1.DB5
  N12: Onderdeel1.D5_PWM, LCD1.DB4
  N13: Onderdeel1.D6_PWM, J1.pulse
  N14: Onderdeel1.D7_PWM, Part5.S
  N15: Onderdeel1.D22, Part3.S
  N16: Onderdeel1.D31, R4.Pin_0
  N17: Onderdeel1.D33, R3.Pin_0
  N18: Onderdeel1.D36, hc-sr1.Echo
  N19: Onderdeel1.D37, hc-sr1.Trig
  N20: Onderdeel1.D43, Part6.S
  N21: LCD1.V0, R2.wiper
  N22: Part2.S, R3.Pin_1
  N23: Part2.Vin, R4.Pin_1

custom parts:
  KY-028 Digital Temperature Sensor Module: KEYES KY-028 Digital Temperature Sensor Module, used to measure changes in temperature.
  KY-011 Two Color LED Module: KEYES KY-011 Two Color LED Module consist of a common cathode 3mm red/green LED.
  KY-022 Infrared Receiver Module: Arduino IR receiver module KY-022, reacts to 38kHz infrared light.
  KY-018 Photoresistor Module: KY-018 Photoresistor module, used to measure light intensity. It can determine the presence or absence of light.
  KY-015 Temperature & Humidity Sensor Module: KY-015 temperature and humidity sensor module, provides a low-latency serial interface to measure humidity and temperature.
  KY-006 Passive Buzzer Module: Passive Piezoelectric Buzzer Module Keyes KY-006, it can produce a range of sound tones depending on the input frequency.
  Water Level Sensor: A water level sensor. This sensor operates at 3V to 5V. The Sig (signal) pin outputs an analogue signal that is in proportion to the amount of water in contact with the sensor.
