# Fritzing sketch scheme (saved by Fritzing 0.9.3b)
breadboards: 2

parts:
  Onderdeel1 = Arduino Mega 2560 (Rev3)
  INA125P = ina125P [package="DIP16 [THT]"]
  MCP3421 = IC, DIP package, 6 pins [chip_label=MCP3421]  # not connected
  C1 = Ceramic Capacitor [capacitance=10nF package="100 mil [THT, multilayer]"]  # not connected
  Load_Cell1 = Load Cell - Red/white/black/green  # not connected
  Onderdeel2 = Arduino Micro (Rev3)  # not connected
  MCP3422 = IC, DIP package, 6 pins [chip_label=MCP3421]
  C2 = Ceramic Capacitor [capacitance=10nF package="100 mil [THT, multilayer]"]
  Load_Cell2 = Load Cell - Red/white/black/green

nets:
  N1: Onderdeel1.5V, INA125P.V+
  N2: Onderdeel1.GND, INA125P.SLEEP
  N3: MCP3422.pin1, C2.1, Load_Cell2.wire4
  N4: MCP3422.pin2, Load_Cell2.wire3
  N5: MCP3422.pin5, Load_Cell2.wire1
  N6: MCP3422.pin6, C2.0, Load_Cell2.wire2

custom parts:
  ina125P: High accuracy instrumentation amplifier.
  Load Cell - Red/white/black/green: A rectangle load cell/weighting pressure Sensor with four wires - Red, white, black, green. Normally corresponding with E+, E-, A+, A- respectively.
