# Fritzing sketch scheme_2wire (saved by Fritzing 0.9.3b)
breadboards: 1

parts:
  Onderdeel2 = Arduino Micro (Rev3)  # not connected
  MCP3422 = IC, DIP package, 6 pins [chip_label=MCP3421]
  C2 = Ceramic Capacitor [capacitance=10nF package="100 mil [THT, multilayer]"]
  Load_Cell2 = Load Cell - Red/white/black/green
  Onderdeel3 = Arduino Micro (Rev3)  # not connected
  Onderdeel4 = Arduino Micro (Rev3)  # not connected
  C1 = Ceramic Capacitor [capacitance=100nF package="100 mil [THT, multilayer]"]

nets:
  N1: MCP3422.pin1, C2.1, Load_Cell2.wire4
  N2: MCP3422.pin5, Load_Cell2.wire1, C1.0
  N3: MCP3422.pin6, C2.0, Load_Cell2.wire2
  N4: Load_Cell2.wire3, C1.1

custom parts:
  Load Cell - Red/white/black/green: A rectangle load cell/weighting pressure Sensor with four wires - Red, white, black, green. Normally corresponding with E+, E-, A+, A- respectively.
